// Logisim project braile.circ as structural Verilog: 2 circuits, main circuit main
module main (
  input  in_1,
  input  in_2,
  input  in_3,
  input  in_4,
  input  in_5,
  input  in_6,
  input  in_7,
  input  in_8
);

  _1 u_1_1 (.out_5(in_1));  // open: in_1, in_2, in_3, in_4, out_6, out_7, out_8, out_9
endmodule

module _1 (
  input  in_1,
  input  in_2,
  input  in_3,
  input  in_4,
  output out_5,
  output out_6,
  output out_7,
  output out_8,
  output out_9
);

  wire not_1_out, not_2_out, not_3_out, not_4_out, not_5_out, not_6_out, not_7_out, not_8_out, not_9_out,
       not_10_out;

  not not_1 (not_1_out, in_2);
  not not_2 (not_2_out, in_3);
  not not_3 (not_3_out, in_1);
  not not_4 (not_4_out, in_4);
  not not_5 (not_5_out, in_1);
  not not_6 (not_6_out, in_3);
  not not_7 (not_7_out, in_1);
  not not_8 (not_8_out, in_4);
  not not_9 (not_9_out, in_1);
  not not_10 (not_10_out, in_1);
  and and_1 (out_5, in_4, in_3, not_1_out, not_3_out);
  and and_2 (out_6, not_4_out, not_2_out, in_2, not_5_out);
  and and_3 (out_7, in_4, not_6_out, in_2, not_7_out);
  and and_4 (out_8, not_8_out, in_3, in_2, not_9_out);
  and and_5 (out_9, in_4, in_3, in_2, not_10_out);

  // Notes on the sheet:
  //   Entradas fora do sub
  //   0011 | Saída para o 0 a 9
  //   0100 | A até O, maiúsculo
  //   0101 | P+, maiúsculo
  //   0110 | A até O, minusculo
  //   0111 | P+, minusculo
endmodule
